# Fritzing sketch Hydroponics (saved by Fritzing 0.9.3b)
perfboards: 1

parts:
  Part1 = Arduino Uno (Rev3)
  J1 = Screw terminal - 2 pins [package=THT]
  R1 = Resistor [tolerance=±5% resistance=220 package=THT]  # not connected
  R2 = Resistor [tolerance=±5% resistance=10k package=THT]  # not connected
  R3 = Photocell (LDR) [package=THT]
  RHT1 = Humidity and Temperature Sensor RHT03
  R4 = Temperature Sensor (Thermistor) [thermistor_type=NTC package=THT]
  U1 = RELAY [package=relay-jzc]
  U2 = RELAY [package=relay-jzc]

nets:
  N1: Part1.A0, U1.NC
  N2: Part1.A1, U2.NC
  N3: Part1.D11_PWM/MOSI, R3.pin_1
  N4: Part1.D12/MISO, R4.pin_1
  N5: Part1.D13/SCK, RHT1.Data-signal
  N6: Part1.3V3, J1.pin2, RHT1.GND_1, U1.NO
  5V: Part1.5V, J1.pin1, R3.pin_0, RHT1.Vcc, R4.pin_0, U2.COIL2
